# Fritzing sketch Light_Sensor_With_LED_Indicator (saved by Fritzing 0.9.3b)
breadboards: 1

parts:
  Componente1 = Arduino Uno (Rev3)
  LED1 = LED - 5mm [color="Red (633nm)" package="5 mm [THT]"]
  R1 = Resistor [tolerance=±5% resistance=330 package=THT]
  LED2 = LED - 5mm [color="Green (570nm)" package="5 mm [THT]"]
  R2 = Resistor [tolerance=±5% resistance=330 package=THT]
  Grove1 = Grove Light Sensor

nets:
  N1: Componente1.A0, Grove1.SIG
  N2: Componente1.D12/MISO, R2.Pin_1
  N3: Componente1.D13/SCK, R1.Pin_0
  GND: Componente1.GND, LED1.cathode, LED2.cathode, Grove1.GND
  5V: Componente1.5V, Grove1.VCC
  N4: LED1.anode, R1.Pin_1
  N5: LED2.anode, R2.Pin_0
